# Fritzing sketch Calendario_Temperatura_Humedad_TFT (saved by Fritzing 0.9.4)
breadboards: 2

parts:
  MH-ET_LIVE_ESP32_DEVKIT1 = MH-ET LIVE ESP32 DEVKIT 38 pins
  DHT1 = DHT22 Humidity and Temperature Sensor
  LCD1 = 2.8" SPI TFT Module [part_number=MSP2807]
  J11 = Screw terminal - 2 pins [package=THT]
  J12 = Screw terminal - 2 pins [package=THT]
  J13 = Screw terminal - 2 pins [package=THT]

nets:
  3V3: MH-ET_LIVE_ESP32_DEVKIT1.3V3, DHT1.VDD, LCD1.pin1, LCD1.pin8
  N1: MH-ET_LIVE_ESP32_DEVKIT1.GND#58, MH-ET_LIVE_ESP32_DEVKIT1.GND#70, DHT1.GND, LCD1.pin2, J11.pin2
  N2: MH-ET_LIVE_ESP32_DEVKIT1.5V, J11.pin1
  N3: MH-ET_LIVE_ESP32_DEVKIT1.IO23, LCD1.pin6, LCD1.pin12, LCD1.pin17, J12.pin2
  N4: MH-ET_LIVE_ESP32_DEVKIT1.IO22, DHT1.DATA
  N5: MH-ET_LIVE_ESP32_DEVKIT1.IO21, LCD1.pin11
  N6: MH-ET_LIVE_ESP32_DEVKIT1.IO19, LCD1.pin13, LCD1.pin16, J13.pin1
  N7: MH-ET_LIVE_ESP32_DEVKIT1.IO18, LCD1.pin7, LCD1.pin10, LCD1.pin15, J13.pin2
  N8: MH-ET_LIVE_ESP32_DEVKIT1.IO5, LCD1.pin18, J12.pin1
  N9: MH-ET_LIVE_ESP32_DEVKIT1.IO4, LCD1.pin4
  N10: MH-ET_LIVE_ESP32_DEVKIT1.IO2, LCD1.pin5
  N11: MH-ET_LIVE_ESP32_DEVKIT1.IO15, LCD1.pin3

custom parts:
  MH-ET LIVE ESP32 DEVKIT 38 pins: http://mh.nodebb.com/topic/2/mh-et-live-esp32-devkit
  2.8" SPI TFT Module: A generic 2.8 inch LCD TFT 320x240 display with touchscreen and SD card slot. Uses the ILI9341 controller, like the Adafruit displays of this size uses.

// code stored in the sketch: baseDatos.h
/*
 * Conexión con la base de datos y envío de la información
 * 24/03/2021
 */
#include <HTTPClient.h>
#include "dht.h"
HTTPClient http; // Se crea el objeto http para el envío de datos

void enviarBD()
{
  // Llamamos a la funcion temperatura para leer las variables de temperatura, humedad y el cálculo de la senación térmica
  temperatura();
  String datos = ("t=" + Temp + "&h=" + Hum + "&st=" + TeR + "&ub=" + ub);
  http.begin(url);                                                     // Iniciamos la conexión http con la dirección web donde esta la páguina que nos inserta los datos
  http.addHeader("Content-Type", "application/x-www-form-urlencoded"); // tipo de datos que enviamos
  String httpRequestData = datos;                                      // enviamos los datos por POST
  int httpResponseCode = http.POST(httpRequestData);                   // leemos la respuesta del servidor
  http.end();                                                          // cerramos la conexión http
}

// code stored in the sketch: configuracion.h

/* Fichero de configuración para el reloj con envío de datos por POST y actualización via OTA
 * Creado el 27/12/2023
 * por @JMTS
*/

// Configuración de la Ubicación
// tambien da nombre al puerto de actualizacion via OTA

byte ub = 3;// Ubicación (1-despacho) (2-salon) (3-pruebas)

char* ubicacion(){
  char *ubic;
  if (ub == 1)
  {
    ubic = "Despacho";
  }
  else if (ub == 2)
  {
    ubic = "Salon";
  }
  else if (ub == 3)
  {
    ubic = "Pruebas";
  }
  return ubic;
}

//Configuración de la WiFi
const char *ssid = "JMTS";
const char *password = "JAVIER276MTS";

//Password para la actualización via OTA
char *passwordOTA = "JavierMt5*/";

//Configuración del Servidor Web
String dominio = "sensores.jmts.es";                            // Dominio que estes usando
String url = "http://" + dominio + "/config/insertar_post.php"; // Dirección web del servidor con el dominio insertado

// code stored in the sketch: ota.h
/*
 * 16/06/2021
*/

#include <ArduinoOTA.h>

void actualizacionOTA(){

// ACTUALIZACIONES VIA OTA
// Establecemos el nombre del dispositivo por la ubicación
ArduinoOTA.setHostname(ubicacion());
// Establecemos una contraseña para autentificar la actualización
ArduinoOTA.setPassword(passwordOTA);

ArduinoOTA
    .onStart([]() {
      String type;
      if (ArduinoOTA.getCommand() == U_FLASH)
        type = "sketch";
      else // U_SPIFFS
        type = "filesystem";

      // NOTA: si actualiza SPIFFS, este sería el lugar para desmontar SPIFFS usando SPIFFS.end ()
      Serial.println("Start updating " + type);
    })
    .onEnd([]() {
      Serial.println("\nEnd");
    })
    .onProgress([](unsigned int progress, unsigned int total) {
      Serial.printf("Progress: %u%%\r", (progress / (total / 100)));
    })
    .onError([](ota_error_t error) {
      Serial.printf("Error[%u]: ", error);
      if (error == OTA_AUTH_ERROR)
        Serial.println("Auth Failed");
      else if (error == OTA_BEGIN_ERROR)
        Serial.println("Begin Failed");
      else if (error == OTA_CONNECT_ERROR)
        Serial.println("Connect Failed");
      else if (error == OTA_RECEIVE_ERROR)
        Serial.println("Receive Failed");
      else if (error == OTA_END_ERROR)
        Serial.println("End Failed");
    });

ArduinoOTA.begin();

Serial.println("Ready");
Serial.print("IP address: ");
Serial.println(WiFi.localIP());
}

// code stored in the sketch: Reloj_Temperatura_Humedad_BaseDatos_OTA.ino
/*
 * @JMTS
 * Probado con ESP32 DEVKIT y WEMOS D1 R32 (palaca con forma de arduino 1 para que funcione hay que realizar las modificaciones descritas en la libreria TFT_eSPI)
 * Reloj con fecha y hora más sensor de temperatura y humedad en pantalla TFT con la libreria TFT_eSPI
 * Sensor de Temperatura-Humedad DHT22 o DHT11 solo has de configurarlo en su script
 * Hora a traves de servidor NTP basado en el ejemplo SimpleTime de la libreria del ESP32
 * Conexión a base de datos Mysql mediante php con el método POST para realizar un registro
 * Actualización del frimware via OTA con contraseña basado en el ejemplo ArduinoOTA
 * 27/12/2024
 *                          NOTA IMPORTANTES
 * El orden en el que se ponen los includes es muy importante, siempre han de ir primero los primeros que se llaman
 */
#include "configuracion.h"
#include "sensorDHT.h"
#include "reloj.h"
#include "tft.h"
#include "conexionWiFi.h"
#include "baseDatos.h"
#include "ota.h"

#define LED_PIN 2 // Led integrado en el PIN2

// Iniciamos los contadores para insertar en la base de datos y actualizar el reloj
unsigned long previosMillis;
unsigned long intervalo = 60000;

void setup()
{
  pinMode(LED_PIN, OUTPUT);
  digitalWrite(LED_PIN, LOW); // Turn onboard LED OFF
  
  dht.begin();

  // Llamamos a la función para configurar la pantalla
  configuracionPantalla();

  // Conexion a la wifi y sincronización del reloj NTP
  conectarWiFi();

  // Configuramos la actualización via OTA
  actualizacionOTA();
}
void loop()
{
  //Si se ha perdido la conexión wifi llamamos a la función para conectar de nuevo y configuramos fecha y hora
  if (WiFi.isConnected() == false){
    conectarWiFi();
    }
  mostrarPantalla();

  unsigned long currentMillis = millis();   
  // Llamamos, cada minuto, a la función para insertar los datos en la base de datos
  if ((unsigned long) (currentMillis - previosMillis) >= intervalo){
      //enviarBD();
      previosMillis = millis();
    }
    ArduinoOTA.handle(); //Llamamos a la actualización via OTA
}

// code stored in the sketch: sensorDHT.h
/*
 / Configuración y función para la toma de datos de un sensor DHT, esta probado con DHT11 y DHT22 en Esp32 Dev Module
 / creado por JMTS
 / EL 27/12/2024
*/

#include <DHT.h>

#define DHTTYPE DHT11
#define DHTPIN 22     // Se define el puerto al que conectamos el Sensor DHT: pin digital 27

DHT dht(DHTPIN, DHTTYPE); // Objeto DHT

double h;
String Hum;
double t;
String Temp;
char g;
char p;
double hic;
String TeR;
String t1;
String t2;
String t3;



void temperatura(){
   h = dht.readHumidity();                  //Leemos la humedad del sensor
   Hum = String(h, 1);                      // La convertimos a un String
   t = dht.readTemperature();               // Leemos la temperatura del sensor
   Temp = String(t, 2);                     // La convertimos a un String
   g = (char)0xF7;                          // Generamos el simbolo de grados centigrados para mostrar en la TFT
   p = '%';                                 // Simbolo de % para mostrar por el LCD
   hic = dht.computeHeatIndex(t, h, false); // Calculamos la sensación térmica
   TeR = String(hic, 2);                    // La convertimos a un String
   t1=("Tem:" + Temp + g);                  // Se crea la cadena de la temperatura
   t2=("Hum:" + Hum + p);                   // Se crea la cadena de la humedad
   t3=("Sen.Ter.:" + TeR + g);             // Se crea la cadena de la sensacion termica
}

// code stored in the sketch: tft.h
/*
 * La función de este archivo es mostrar en la pantalla TFT los datos que queremos ver.
 * 
 * JMTS
 * 27/12/24
*/

#include <SPI.h>		// incluye libreria bus SPI
#include <Adafruit_GFX.h>	// incluye libreria para manejo de graficos
#include <TFT_eSPI.h>

// Objeto TFT 
TFT_eSPI tft = TFT_eSPI();	// crea objeto;
#define GFXFF 1
//definicion de los colores que vamos a utilizar
#define BLACK   0x0000
#define BLUE    0x001F
#define RED     0xF800
#define GREEN   0x07E0
#define CYAN    0x07FF
#define MAGENTA 0xF81F
#define YELLOW  0xFFE0
#define WHITE   0xFFFF

// con esta función dibujamos lo que no queremos que no se refresque en la pantalla y la orientación de esta, la ejecutamos desde la funcion configuracionPantalla().
void zonaFijaPantalla(){

  tft.setRotation(1);				           // establece posicion 1 - vertical pines pantalla abajo, 2-horizontal pines pantalla derecha, 3-vertical pines pantalla arriba, 4-horizontal pines pantalla izquierda.
  tft.fillScreen(BLACK);		           // Establece el fondo de pantalla.
  tft.drawLine(0, 135, 480, 135, RED); // linea horizontal de color rojo
  tft.setCursor(0,180);				         // ubica cursor

}

// Esta funcion se ejecuta en el Setup para configurar la pantalla y mostrar los datos o dibujos que mo se refrescan mediante la función zonaFijaPantalla().
void configuracionPantalla(){
  tft.begin();					               // Inicializa pantalla.
  Serial.begin(115200);                // Se inicializa el puerto serie.
  zonaFijaPantalla();                  // Llamamos a la función para mostrar los datos e imágenes que no se refrescan y permanecen fijos en pantalla.
}

// Función para imprimir los datos que se refrescan en la pantlla
void mostrarPantalla(){
  temperatura();                                        // Recojemos los datos de temperatura, humedad y sensación térmica.
  fecha();                                              // Recojemos los datos de fecha y hora
  tft.setCursor(150,15);                                // Posicionamos el cursor
  tft.setTextColor(WHITE, BLACK);                       // Establece el color de texto y del fondo para el texto
  tft.setTextSize(8);                                   // Establecemos el tamaño del texto para esta linea
  tft.print(horMin);
  tft.setCursor(65,90);				                          // posicionamos el curos
  tft.setTextSize(4);                                   // Establece el tamaño de la fuente
  tft.print(diaS + " " + dia + " " + mes + " " + ano);  // Imprimimos la fecha
  tft.setTextColor(YELLOW, BLACK);                      // texto en color amarillo y fondo negro.
  tft.setCursor(0,150);		                              // Posicionamos el cursor
  tft.print(t1 + " " + t2);		                          // Imprimimos la temperatura y la humedad
  tft.setCursor(65,205);				                        // Posicionamos el cursor
  tft.print(t3);                                        // Imprimimos la Sensación Térmica
}
